# Fritzing sketch ece110sketch (saved by Fritzing 0.7.10b)
breadboards: 1

parts:
  M1 = DC Motor
  DC_Motor = DC Motor
  J1 = Infrared Proximity Sensor
  J2 = Infrared Proximity Sensor
  J3 = Infrared Proximity Sensor
  J4 = Infrared Proximity Sensor
  J5 = Infrared Proximity Sensor
  J6 = Infrared Proximity Sensor
  Q1 = NPN-Transistor [package="TO92 [THT]"]
  VCC1 = Battery
  Adafruit_Atmega32u1 = Adafruit Atmega32u4 Breakout Board [part_number="Atmega 32u4"]
  U1 = Voltage Regulator - 5V [package="TO220 [THT]"]
  Q2 = NPN-Transistor [package="TO92 [THT]"]

nets:
  N1: M1.pin_1, Q1.C
  N2: M1.pin_2, DC_Motor.pin_2, VCC1.-, Adafruit_Atmega32u1.GND#36, U1.GND
  N3: DC_Motor.pin_1, Q2.C
  N4: J1.Vout, Adafruit_Atmega32u1.F1
  N5: J2.Vout, Adafruit_Atmega32u1.F4
  N6: J3.Vout, Adafruit_Atmega32u1.F5
  N7: J4.Vout, Adafruit_Atmega32u1.F6
  N8: J5.Vout, Adafruit_Atmega32u1.F7
  N9: J6.Vout, Adafruit_Atmega32u1.F0
  N10: Q1.E, VCC1.+, U1.input_voltage, Q2.E
  N11: Q1.B, Adafruit_Atmega32u1.D6
  N12: Adafruit_Atmega32u1.5V, U1.output_voltage
  N13: Adafruit_Atmega32u1.D5, Q2.B

notes:
  Left Motor
  Right Motor
